# Fritzing sketch Schematic (saved by Fritzing 0.9.3b)
breadboards: 1

parts:
  LCD_Display_16x2 = LCD screen
  Arduino_Uno_R3_Controller_Board = Arduino Uno (Rev3)
  Potentiometer = Trimmer Potentiometer [maximum_resistance=10kΩ package=THT]
  Blue_LED_Light = LED - 5mm [color="Red (633nm)" package="5 mm [THT]"]
  3x330Ω_Resistor = Resistor [tolerance=±5% resistance=330 package="0603 [SMD]"]
  White_LED_Light = LED - 5mm [color="White (6500K)" package="5 mm [THT]"]
  Red_LED_Light = LED - 5mm [color="Blue (430nm)" package="5 mm [THT]"]
  R3 = Resistor [tolerance=±5% resistance=330 package="0603 [SMD]"]
  R4 = Resistor [tolerance=±5% resistance=330 package="0603 [SMD]"]
  DHT11_Temp_&_Humidity_Sensor = DHT11 Humitidy and Temperature Sensor (3 pins)

nets:
  GND: LCD_Display_16x2.VSS, LCD_Display_16x2.R/W, LCD_Display_16x2.LED-, Arduino_Uno_R3_Controller_Board.GND, Potentiometer.leg2, Blue_LED_Light.cathode, White_LED_Light.cathode, Red_LED_Light.cathode, DHT11_Temp_&_Humidity_Sensor.Gnd
  VDD: LCD_Display_16x2.VDD, LCD_Display_16x2.LED+, Arduino_Uno_R3_Controller_Board.5V, Potentiometer.leg1, DHT11_Temp_&_Humidity_Sensor.Plus
  N1: LCD_Display_16x2.V0, Potentiometer.wiper
  N2: LCD_Display_16x2.RS, Arduino_Uno_R3_Controller_Board.D1/TX
  N3: LCD_Display_16x2.E, Arduino_Uno_R3_Controller_Board.D2
  N4: LCD_Display_16x2.DB4, Arduino_Uno_R3_Controller_Board.D4
  N5: LCD_Display_16x2.DB5, Arduino_Uno_R3_Controller_Board.D5_PWM
  N6: LCD_Display_16x2.DB6, Arduino_Uno_R3_Controller_Board.D6_PWM
  N7: LCD_Display_16x2.DB7, Arduino_Uno_R3_Controller_Board.D7
  N8: Arduino_Uno_R3_Controller_Board.D8, DHT11_Temp_&_Humidity_Sensor.Signal
  N9: Arduino_Uno_R3_Controller_Board.D9_PWM, 3x330Ω_Resistor.Pin_0
  N10: Arduino_Uno_R3_Controller_Board.D10_PWM/SS, R3.Pin_0
  N11: Arduino_Uno_R3_Controller_Board.D11_PWM/MOSI, R4.Pin_0
  N12: Blue_LED_Light.anode, 3x330Ω_Resistor.Pin_1
  N13: White_LED_Light.anode, R3.Pin_1
  N14: Red_LED_Light.anode, R4.Pin_1

custom parts:
  DHT11 Humitidy and Temperature Sensor (3 pins): DHT11 Humidity and Temperature Sensor (3 pins).
